// Logisim project Inversor_de_3_bits.circ as structural Verilog: 1 circuit, main circuit main
module main (
  input  [2:0] in_1,
  input  e3,
  output [2:0] s0__s1__s2
);

  xor xor_1 (s0__s1__s2[0], in_1[0], e3);
  xor xor_2 (s0__s1__s2[1], in_1[1], e3);
  xor xor_3 (s0__s1__s2[2], in_1[2], e3);

  // Notes on the sheet:
  //   ei    ek    si
  //   0      0      0
  //   0      1      1
  //   1      0      1
  //   1      1      0
  //   e0, e1, e2
endmodule
