// Logisim project Sumador_Completo_de_3_bits.circ as structural Verilog: 1 circuit, main circuit main
module main (
  input  B0,
  input  A0,
  input  C_in,
  input  B1,
  input  A1,
  input  B2,
  input  A2,
  output out_8,
  output out_9,
  output C_out,
  output out_11
);

  wire and_1_out, and_2_out, and_3_out, and_4_out, and_5_out, and_6_out, or_1_out, or_2_out, xor_1_out,
       xor_3_out, xor_5_out;

  or or_1 (or_1_out, and_1_out, and_2_out);
  or or_2 (or_2_out, and_3_out, and_4_out);
  or or_3 (C_out, and_5_out, and_6_out);
  and and_1 (and_1_out, B0, A0);
  and and_2 (and_2_out, xor_1_out, C_in);
  and and_3 (and_3_out, B1, A1);
  and and_4 (and_4_out, xor_3_out, or_1_out);
  and and_5 (and_5_out, B2, A2);
  and and_6 (and_6_out, xor_5_out, or_2_out);
  xor xor_1 (xor_1_out, B0, A0);
  xor xor_2 (out_8, xor_1_out, C_in);
  xor xor_3 (xor_3_out, B1, A1);
  xor xor_4 (out_9, xor_3_out, or_1_out);
  xor xor_5 (xor_5_out, B2, A2);
  xor xor_6 (out_11, xor_5_out, or_2_out);

  // Notes on the sheet:
  //   (A0 ⋅ B0) + (Cin ⋅ (A0 ⊕ B0))
  //   C1
  //   (A1 ⋅ B1) + (C1 ⋅ (A1 ⊕ B1))
  //   C2
  //   (A ⋅ B) + (Cin ⋅ (A ⊕ B))
  //   S0 = A0 ⊕ B0 ⊕ Cin
  //   S1 = A1 ⊕ B1 ⊕ C1
  //   S2 = A2 ⊕ B2 ⊕ C2
endmodule
