// Logisim project Sumador_Completo_de_4_bits.circ as structural Verilog: 1 circuit, main circuit main
module main (
  input  [3:0] in_1,
  input  [3:0] in_2,
  input  Cin,
  output Cout,
  output [3:0] out_5
);

  wire and_1_out, and_2_out, and_3_out, and_4_out, and_5_out, and_6_out, and_7_out, and_8_out, or_2_out,
       or_3_out, or_4_out, xor_1_out, xor_3_out, xor_5_out, xor_7_out;

  or or_1 (Cout, and_1_out, and_2_out);
  and and_1 (and_1_out, in_1[3], in_2[3]);
  and and_2 (and_2_out, xor_1_out, or_2_out);
  xor xor_1 (xor_1_out, in_1[3], in_2[3]);
  xor xor_2 (out_5[3], xor_1_out, or_2_out);
  or or_2 (or_2_out, and_3_out, and_4_out);
  and and_3 (and_3_out, in_1[2], in_2[2]);
  and and_4 (and_4_out, xor_3_out, or_3_out);
  xor xor_3 (xor_3_out, in_1[2], in_2[2]);
  xor xor_4 (out_5[2], xor_3_out, or_3_out);
  or or_3 (or_3_out, and_5_out, and_6_out);
  and and_5 (and_5_out, in_1[1], in_2[1]);
  and and_6 (and_6_out, xor_5_out, or_4_out);
  xor xor_5 (xor_5_out, in_1[1], in_2[1]);
  xor xor_6 (out_5[1], xor_5_out, or_4_out);
  or or_4 (or_4_out, and_7_out, and_8_out);
  and and_7 (and_7_out, in_1[0], in_2[0]);
  and and_8 (and_8_out, xor_7_out, Cin);
  xor xor_7 (xor_7_out, in_1[0], in_2[0]);
  xor xor_8 (out_5[0], xor_7_out, Cin);

  // Notes on the sheet:
  //   (A ⋅ B) + (Cin ⋅ (A ⊕ B))
  //   S3 = A3 ⊕ B3 ⊕ C3
  //   (A2 ⋅ B2) + (C2 ⋅ (A2 ⊕ B2))
  //   C3
  //   B = (B0, B1, B2, B3)
  //   A = (A0, A1, A2, A3)
  //   S2 = A2 ⊕ B2 ⊕ C2
  //   (A1 ⋅ B1) + (C1 ⋅ (A1 ⊕ B1))
  //   C2
  //   S = (S0, S1, S2, S3)
  //   S1 = A1 ⊕ B1 ⊕ C1
  //   (A0 ⋅ B0) + (Cin ⋅ (A0 ⊕ B0))
  //   C1
  //   S0 = A0 ⊕ B0 ⊕ Cin
endmodule
