// Logisim project Sumador_Simple.circ as structural Verilog: 1 circuit, main circuit main
module main (
  input  in_1,
  input  in_2,
  output Carry,
  output Sum
);

  and and_1 (Carry, in_2, in_1);
  xor xor_1 (Sum, in_1, in_2);

  // Notes on the sheet:
  //   A   B   Sum  Carry
  //   0   0       0         0
  //   0   1       1         0
  //   1   0       1         0
  //   1   1       0         1
endmodule
