// Logisim project combinacionales.circ as structural Verilog: 11 circuits, main circuit verificador
module sumador_simple (
  input  A,
  input  B,
  output S,
  output Cout
);

  and and_1 (Cout, B, A);
  xor xor_1 (S, A, B);
endmodule

module sumador_completo (
  input  Cin,
  input  A,
  input  B,
  output S,
  output Cout
);

  wire and_1_out, and_2_out, xor_1_out;

  and and_1 (and_1_out, B, A);
  xor xor_1 (xor_1_out, A, B);
  or or_1 (Cout, and_1_out, and_2_out);
  and and_2 (and_2_out, xor_1_out, Cin);
  xor xor_2 (S, Cin, xor_1_out);
endmodule

module sumador_4 (
  input  Cin,
  input  [3:0] A,
  input  [3:0] B,
  output [3:0] S,
  output Cout
);

  wire and_1_out, and_2_out, and_3_out, and_4_out, and_5_out, and_6_out, and_7_out, and_8_out, or_1_out,
       or_2_out, or_3_out, xor_1_out, xor_2_out, xor_3_out, xor_4_out;

  and and_1 (and_1_out, B[0], A[0]);
  and and_2 (and_2_out, B[1], A[1]);
  and and_3 (and_3_out, B[2], A[2]);
  and and_4 (and_4_out, B[3], A[3]);
  xor xor_1 (xor_1_out, A[0], B[0]);
  or or_1 (or_1_out, and_1_out, and_5_out);
  xor xor_2 (xor_2_out, A[1], B[1]);
  or or_2 (or_2_out, and_2_out, and_6_out);
  xor xor_3 (xor_3_out, A[2], B[2]);
  or or_3 (or_3_out, and_3_out, and_7_out);
  xor xor_4 (xor_4_out, A[3], B[3]);
  or or_4 (Cout, and_4_out, and_8_out);
  and and_5 (and_5_out, xor_1_out, Cin);
  and and_6 (and_6_out, xor_2_out, or_1_out);
  and and_7 (and_7_out, xor_3_out, or_2_out);
  and and_8 (and_8_out, xor_4_out, or_3_out);
  xor xor_5 (S[0], Cin, xor_1_out);
  xor xor_6 (S[1], or_1_out, xor_2_out);
  xor xor_7 (S[2], or_2_out, xor_3_out);
  xor xor_8 (S[3], or_3_out, xor_4_out);
  Hex_Digit_Display hex_digit_display_1 (.value(S));  // open: dp

  // Other names for the same wires on the sheet: EA1 = A[0]; EB1 = A[1]; EC1 = A[2]; ED1 = A[3]; EA2 = B[0];
  //   EB2 = B[1]; EC2 = B[2]; ED2 = B[3]; SA = S[0]; SB = S[1]; SC = S[2]; SD = S[3]

  // Notes on the sheet:
  //   C1
  //   C2
  //   C3
  //   (E1 ⋅ E2) + (Cin ⋅ (E1 ⊕ E2))
  //   (EA1 ⋅ EA2) + (Cin ⋅ (EA1 ⊕ EA2))
  //   (EB1 ⋅ EB2) + (C1 ⋅ (EB1 ⊕ EB2))
  //   (EC1 ⋅ EC2) + (C2 ⋅ (EC1 ⊕ EC2))
  //   EA1 ⊕ EA2 ⊕ Cin
  //   EB1 ⊕ EB2 ⊕ C1
  //   EC1 ⊕ EC2 ⊕ C2
  //   ED1 ⊕ ED2 ⊕ C3
endmodule

module comparador_cero (
  input  [3:0] A,
  output Z
);

  wire or_1_out, or_2_out, or_3_out;

  or or_1 (or_1_out, A[0], A[1]);
  or or_2 (or_2_out, A[2], A[3]);
  or or_3 (or_3_out, or_1_out, or_2_out);
  not not_1 (Z, or_3_out);

  // Notes on the sheet:
  //   H1 = A0 ⊕ A1
  //   H0 = A2 ⊕ A3
  //   H2 = H0 ⊕ H1
  //   H2 NEGADO
endmodule

module sumador_flags (
  input  Cin,
  input  [3:0] A,
  input  [3:0] B,
  output [3:0] S,
  output N,
  output Z,
  output V,
  output C
);

  wire and_1_out, and_2_out, and_3_out, and_4_out, and_5_out, and_6_out, and_7_out, and_8_out, CA, CB, CC,
       or_5_out, or_6_out, or_7_out, xor_1_out, xor_2_out, xor_3_out, xor_4_out;

  and and_1 (and_1_out, B[0], A[0]);
  and and_2 (and_2_out, B[1], A[1]);
  and and_3 (and_3_out, B[2], A[2]);
  and and_4 (and_4_out, B[3], A[3]);
  xor xor_1 (xor_1_out, A[0], B[0]);
  or or_1 (CA, and_1_out, and_5_out);
  xor xor_2 (xor_2_out, A[1], B[1]);
  or or_2 (CB, and_2_out, and_6_out);
  xor xor_3 (xor_3_out, A[2], B[2]);
  or or_3 (CC, and_3_out, and_7_out);
  xor xor_4 (xor_4_out, A[3], B[3]);
  or or_4 (C, and_4_out, and_8_out);
  and and_5 (and_5_out, xor_1_out, Cin);
  and and_6 (and_6_out, xor_2_out, CA);
  and and_7 (and_7_out, xor_3_out, CB);
  and and_8 (and_8_out, xor_4_out, CC);
  xor xor_5 (S[0], Cin, xor_1_out);
  xor xor_6 (S[1], CA, xor_2_out);
  xor xor_7 (S[2], CB, xor_3_out);
  xor xor_8 (N, CC, xor_4_out);
  or or_5 (or_5_out, S[0], S[1]);
  or or_6 (or_6_out, S[2], N);
  xor xor_9 (V, C, CC);
  Hex_Digit_Display hex_digit_display_1 (.value({N, S[2:0]}));  // open: dp
  not not_1 (Z, or_7_out);
  or or_7 (or_7_out, or_5_out, or_6_out);
  comp_overflow comp_overflow_1 (.c3(N), .a3(A[3]), .b3(B[3]), .O(V));

  assign S[3] = N;

  // Other names for the same wires on the sheet: EA1 = A[0]; EB1 = A[1]; EC1 = A[2]; ED1 = A[3]; EA2 = B[0];
  //   EB2 = B[1]; EC2 = B[2]; ED2 = B[3]; SA = S[0]; SB = S[1]; SC = S[2]; SD = N

  // Notes on the sheet:
  //   C1
  //   C2
  //   C3
  //   (EA1 ⋅ EA2) + (Cin ⋅ (EA1 ⊕ EA2))
  //   (EB1 ⋅ EB2) + (C1 ⋅ (EB1 ⊕ EB2))
  //   (EC1 ⋅ EC2) + (C2 ⋅ (EC1 ⊕ EC2))
  //   EA1 ⊕ EA2 ⊕ Cin
  //   EB1 ⊕ EB2 ⊕ C1
  //   EC1 ⊕ EC2 ⊕ C2
  //   ED1 ⊕ ED2 ⊕ C3
  //   H0 = SA ⊕ SB
  //   H1 = SC ⊕ SD
  //   H2 = H0 ⊕ H1
endmodule

module incrementador_4 (
  input  [3:0] A,
  output [3:0] S
);

  sumador_4 sumador_4_1 (.A(A), .B(4'b0001), .S(S));  // open: Cin, Cout
  Hex_Digit_Display hex_digit_display_1 (.value(S));  // open: dp
endmodule

module inversor_4 (
  input  [3:0] A,
  input  INV,
  output [3:0] S
);

  wire [3:0] incrementador_4_1_s, not_1_out;

  not not_1 (not_1_out[0], A[0]);
  not not_2 (not_1_out[1], A[1]);
  not not_3 (not_1_out[2], A[2]);
  not not_4 (not_1_out[3], A[3]);
  Multiplexer #(.width(4)) multiplexer_1 (.in0(A), .in1(incrementador_4_1_s), .out(S), .sel(INV));
  incrementador_4 incrementador_4_1 (.A(not_1_out), .S(incrementador_4_1_s));
  Hex_Digit_Display hex_digit_display_1 (.value(S));  // open: dp
endmodule

module ALU (
  input  [3:0] A,
  input  [3:0] B,
  input  [1:0] OP,
  output N,
  output Z,
  output V,
  output C,
  output [3:0] S
);

  wire BORR_RES, C_RES, C_SUM, comparador_cero_3_z, N_AND, N_OR, N_RES, N_SUM, NOT_C, V_RES, V_RES_OVER,
       V_SUM, Z_AND, Z_OR, Z_RES, Z_SUM;
  wire [3:0] A_RES_B, NEG_B, S_AND, S_OR, S_RES, S_SUM;

  Multiplexer multiplexer_1 (.in0(1'b0), .in1(1'b1), .out(N_AND), .sel(S_AND[3]));
  and and_1 (S_AND[0], A[0], B[0]);
  and and_2 (S_AND[1], A[1], B[1]);
  and and_3 (S_AND[2], A[2], B[2]);
  and and_4 (S_AND[3], A[3], B[3]);
  Multiplexer multiplexer_2 (.in0(NOT_C), .in1(1'b0), .out(BORR_RES), .sel(comparador_cero_3_z));
  inversor_4 inversor_4_1 (.A(B), .INV(1'b1), .S(NEG_B));
  sumador_flags sumador_flags_1 (.Cin(1'b0), .A(A), .B(B), .S(S_SUM), .N(N_SUM), .Z(Z_SUM), .V(V_SUM), .C(C_SUM));
  sumador_flags sumador_flags_2 (.Cin(1'b0), .A(A), .B(NEG_B), .S(S_RES), .N(N_RES), .Z(Z_RES), .V(V_RES), .C(C_RES));
  comparador_cero comparador_cero_1 (.A(S_AND), .Z(Z_AND));
  comparador_cero comparador_cero_2 (.A(S_OR), .Z(Z_OR));
  comparador_cero comparador_cero_3 (.A(B), .Z(comparador_cero_3_z));
  Multiplexer #(.width(4)) multiplexer_3 (.in0(S_RES), .in1(A), .out(A_RES_B), .sel(comparador_cero_3_z));
  Multiplexer multiplexer_4 (.in0(1'b0), .in1(1'b1), .out(N_OR), .sel(S_OR[3]));
  or or_1 (S_OR[0], A[0], B[0]);
  or or_2 (S_OR[1], A[1], B[1]);
  or or_3 (S_OR[2], A[2], B[2]);
  or or_4 (S_OR[3], A[3], B[3]);
  not not_1 (NOT_C, C_RES);
  Multiplexer #(.select(2), .width(4)) multiplexer_5 (
    .in0(S_SUM), .in1(A_RES_B), .in2(S_AND), .in3(S_OR), .out(S), .sel(OP));
  Multiplexer #(.select(2)) multiplexer_6 (.in0(N_SUM), .in1(N_RES), .in2(N_AND), .in3(N_OR), .out(N), .sel(OP));
  Multiplexer #(.select(2)) multiplexer_7 (.in0(Z_SUM), .in1(Z_RES), .in2(Z_AND), .in3(Z_OR), .out(Z), .sel(OP));
  Multiplexer #(.select(2)) multiplexer_8 (.in0(V_SUM), .in1(V_RES_OVER), .in2(1'b0), .in3(1'b0), .out(V), .sel(OP));
  Multiplexer #(.select(2)) multiplexer_9 (.in0(C_SUM), .in1(BORR_RES), .in2(1'b0), .in3(1'b0), .out(C), .sel(OP));
  overflow_resta overflow_resta_1 (.V_in(V_RES), .B(B), .V_out(V_RES_OVER));
  Hex_Digit_Display hex_digit_display_1 (.value(S));  // open: dp
endmodule

module verificador (
  output [3:0] out_1,
  output [3:0] out_2,
  output [1:0] out_3,
  output halt,
  output N,
  output Z,
  output V,
  output C,
  output [3:0] res
);

  wire clock_1_out;

  Clock clock_1 (.out(clock_1_out));
  Counter #(.max('h3ff), .width(10)) counter_1 (
    .clk(clock_1_out), .carry(halt), .Q({out_3, out_2, out_1}));  // open: clr, load, up, count, D
  ALU alu_1 (.A(out_1), .B(out_2), .OP(out_3), .N(N), .Z(Z), .V(V), .C(C), .S(res));
endmodule

module overflow_resta (
  input  V_in,
  input  [3:0] B,
  output V_out
);

  wire comparador_cero_1_z, not_2_out;
  wire [3:3] not_1_out;

  not not_1 (not_1_out[3], B[3]);
  not not_2 (not_2_out, V_in);
  comparador_cero comparador_cero_1 (.A({not_1_out[3], B[2:0]}), .Z(comparador_cero_1_z));
  Multiplexer multiplexer_1 (.in0(V_in), .in1(not_2_out), .out(V_out), .sel(comparador_cero_1_z));
endmodule

module comp_overflow (
  input  c3,
  input  a3,
  input  b3,
  output O
);

  wire not_1_out, xor_1_out, xor_2_out;

  xor xor_1 (xor_1_out, c3, a3);
  not not_1 (not_1_out, xor_2_out);
  xor xor_2 (xor_2_out, a3, b3);
  and and_1 (O, xor_1_out, not_1_out);
endmodule
